# Fritzing sketch Prototype (saved by Fritzing 0.9.1b)
breadboards: 1

parts:
  CAPTOUCH1 = CAP1188 8-Key Captouch
  ARDUINO1 = Arduino Micro
  CAPTOUCH2 = CAP1188 8-Key Captouch  # not connected
  R1 = Resistor [tolerance=±5% resistance=15 package=THT]
  NEOPIXEL1 = Neopixel Strip -- White (30/m)
  NEOPIXEL2 = Neopixel Strip -- White (30/m)
  C1 = Electrolytic Capacitor [capacitance=1µF package="100 mil [THT, electrolytic]"]
  JACK1 = 2.1mm Barrel Jack with Terminal Block

nets:
  N1: CAPTOUCH1.SDA/MISO, ARDUINO1.D2
  N2: CAPTOUCH1.SCK, ARDUINO1.D3
  GND: CAPTOUCH1.GND, ARDUINO1.GND#31, NEOPIXEL1.GND, NEOPIXEL2.GND, C1.-, JACK1.NEG
  N3: ARDUINO1.D6, R1.Pin_1
  +5V: ARDUINO1.VIN, NEOPIXEL1.+5V, NEOPIXEL2.+5V, C1.+, JACK1.POS
  N4: R1.Pin_0, NEOPIXEL1.Din
  N5: NEOPIXEL1.Dout, NEOPIXEL2.Din

custom parts:
  CAP1188 8-Key Captouch: CAP1188 8-Key Captouch Breakout
  Arduino Micro: Arduino Micro Microcontroller
  Neopixel Strip -- White (30/m): These NeoPixel strips have 30 digitally-addressable pixel LEDs per meter and are very affordable and are only 12.5 mm wide, 10 mm if you remove the strip from the casing.
